# Fritzing sketch connection (saved by Fritzing 0.9.3b)
breadboards: 1

parts:
  Pololu_A1 = Pololu A4988 [package=SO16]
  Part1 = Arduino Nano (Rev3.0)
  M1 = Stepper Motor - Bipolar
  C1 = Electrolytic Capacitor [capacitance=47µF package="100 mil [THT, electrolytic]"]
  S1 = Pushbutton [package="[SMD]"]
  S2 = Pushbutton [package="[SMD]"]
  R1 = Trimmer Potentiometer [maximum_resistance=10kΩ package=THT]
  J1 = Piezo Speaker
  Q1 = NPN-Transistor [package="TO92 [THT]"]
  R2 = Resistor [tolerance=±5% resistance=220 package=THT]
  U1 = RELAY [package=relay-jzc]

nets:
  N1: Pololu_A1.RESET, Pololu_A1.SLEEP
  N2: Pololu_A1.STEP, Part1.D3
  N3: Pololu_A1.DIR, Part1.D2
  N4: Pololu_A1.GND#8, Part1.GND, S1.Pin_1, S1.Pin_2, S2.Pin_3, S2.Pin_4, R1.leg1
  VDD: Pololu_A1.VDD, Part1.5V, R1.leg2
  N5: Pololu_A1.1B, M1.D
  N6: Pololu_A1.1A, M1.B
  N7: Pololu_A1.2A, M1.C
  N8: Pololu_A1.2B, M1.A
  N9: Pololu_A1.GND#14, C1.-, J1.pin1, Q1.C
  N10: Pololu_A1.VMOT, C1.+, U1.MAIN, U1.COIL1
  N11: Part1.D4, S1.Pin_3, S1.Pin_4
  N12: Part1.D5, S2.Pin_1, S2.Pin_2
  N13: Part1.D6, J1.pin2
  N14: Part1.D8, R2.Pin_1
  N15: Part1.A0, R1.wiper
  N16: Q1.E, U1.COIL2
  N17: Q1.B, R2.Pin_0

notes:
  5V on top, then step up converter, 12V on bottom
  Connecting I2C Screen ->>>>>>>>>>
  SDA- green
  SCL - blue
  VCC - white
  GND - black
  Two white cables must be connected to cannon n3 cable. Shutter will be activated when they are compact. In n3 port there are 3 pins, we need to find shutter and gnd pin and connect them to relay . voltage must be connected to relay's coil
